# Fritzing sketch VoltAmpMeterWiring (saved by Fritzing 0.9.1b)
breadboards: 1

parts:
  Shunt = Resistor [tolerance=±5% resistance=0 package=THT]
  Device_Power = female pin header, 2 pins [form="♀ (female)"]
  Device_Measure = female pin header, 3 pins [form="♀ (female)"]
  Load = DC Motor
  PSU_4_5-30v = Battery Holders [package=battcom_20mm_pth]
  Load_Power = Battery Holders [package=battcom_20mm_pth]
  C_(3x) = Electrolytic Capacitor [capacitance=3.3mF voltage=35V package="100 mil [THT, electrolytic]"]

nets:
  N1: Shunt.Pin_0, Device_Measure.pin3
  N2: Shunt.Pin_1, Load.pin_2, C_(3x).-
  N3: Device_Power.pin1, PSU_4_5-30v.+
  N4: Device_Power.pin2, PSU_4_5-30v.-
  N5: Device_Measure.pin1, Load.pin_1, Load_Power.-, C_(3x).+

notes:
  PSU 4.5-30V
